// Logisim project counterTemplates.circ as structural Verilog: 10 circuits, main circuit 4 bit mod counter
module _2__3_bit_mod_counter (
  input  S,
  input  R,
  input  En,
  input  CP,
  output Q2,
  output Q1,
  output Q0,
  output nQ2,
  output nQ1,
  output nQ0
);

  wire and_1_out, and_2_out, or_1_out, or_2_out, or_3_out;

  LED D1 (.in(or_1_out));
  LED D2 (.in(or_3_out));
  LED D0 (.in(or_2_out));
  onPosEdge onposedge_1 ();
  rising_edge_D_FF rising_edge_d_ff_1 (.Q(Q2), .C(CP), .D(or_3_out), .S(S), .R(R), .Enable(1'b1), .nQ(nQ2));
  rising_edge_D_FF rising_edge_d_ff_2 (.Q(Q1), .C(CP), .D(or_1_out), .S(S), .R(R), .Enable(1'b1), .nQ(nQ1));
  rising_edge_D_FF rising_edge_d_ff_3 (.Q(Q0), .C(CP), .D(or_2_out), .S(S), .R(R), .Enable(1'b1), .nQ(nQ0));
  and and_1 (and_1_out, Q2, nQ1);
  and and_2 (and_2_out, nQ2, Q1, Q0);
  or or_1 (or_1_out, nQ1, nQ0);
  or or_2 (or_2_out, Q2, Q1);
  or or_3 (or_3_out, and_1_out, and_2_out);

  // Notes on the sheet:
  //   Aufgabe 2
endmodule

module _3__11_bit_mod_counter (
  output Q3,
  output Q2,
  output Q1,
  output Q0
);

  wire and_1_out, and_2_out, and_3_out, and_4_out, and_5_out, and_6_out, and_7_out, and_8_out, C_out,
       not_1_out, not_2_out, not_3_out, not_4_out, not_5_out, not_6_out, not_7_out, not_8_out, not_9_out,
       or_1_out, or_2_out, or_3_out;

  LED D1 (.in(Q1));
  LED D0 (.in(Q0));
  LED D2 (.in(Q2));
  LED D3 (.in(Q3));
  not not_1 (not_1_out, Q1);
  not not_2 (not_2_out, Q0);
  not not_3 (not_3_out, Q3);
  not not_4 (not_4_out, Q2);
  not not_5 (not_5_out, Q1);
  not not_6 (not_6_out, Q0);
  not not_7 (not_7_out, Q1);
  not not_8 (not_8_out, Q0);
  not not_9 (not_9_out, Q0);
  and and_1 (and_1_out, Q2, Q1, Q0);
  and and_2 (and_2_out, Q3, not_1_out);
  and and_3 (and_3_out, Q3, not_2_out);
  and and_4 (and_4_out, not_3_out, not_4_out, Q1, Q0);
  and and_5 (and_5_out, Q2, not_5_out);
  and and_6 (and_6_out, Q2, not_6_out);
  and and_7 (and_7_out, not_7_out, Q0);
  and and_8 (and_8_out, Q1, not_8_out);
  Clock C (.out(C_out));
  or or_1 (or_1_out, and_1_out, and_2_out, and_3_out);
  or or_2 (or_2_out, and_4_out, and_5_out, and_6_out);
  or or_3 (or_3_out, and_7_out, and_8_out);
  rising_edge_D_FF rising_edge_d_ff_1 (.Q(Q3), .C(C_out), .D(or_1_out), .Enable(1'b1));  // open: S, R, nQ
  rising_edge_D_FF rising_edge_d_ff_2 (.Q(Q2), .C(C_out), .D(or_2_out), .Enable(1'b1));  // open: S, R, nQ
  rising_edge_D_FF rising_edge_d_ff_3 (.Q(Q1), .C(C_out), .D(or_3_out), .Enable(1'b1));  // open: S, R, nQ
  rising_edge_D_FF rising_edge_d_ff_4 (.Q(Q0), .C(C_out), .D(not_9_out), .Enable(1'b1));  // open: S, R, nQ

  // Notes on the sheet:
  //   Aufgabe 3
endmodule

module _4__Forward___Backward_Counter (
  input  F_nB,
  input  R,
  output Q2,
  output Q1,
  output Q0
);

  wire CP_out, n4_sn1_1_q0, n4_sn1_1_q1, n4_sn1_1_q2, n4_sn2_1_r0, n4_sn2_1_r1, n4_sn2_1_r2, n4_sn2_1_s0,
       n4_sn2_1_s1, n4_sn2_1_s2;

  _4__SN1 u_4_sn1_1 (.E2(Q2), .E1(Q1), .E0(Q0), .FB(F_nB), .Q2(n4_sn1_1_q2), .Q1(n4_sn1_1_q1), .Q0(n4_sn1_1_q0));
  _4__SN2 u_4_sn2_1 (
    .FB(F_nB), .R(R), .S2(n4_sn2_1_s2), .S1(n4_sn2_1_s1), .S0(n4_sn2_1_s0), .R2(n4_sn2_1_r2),
    .R1(n4_sn2_1_r1), .R0(n4_sn2_1_r0));
  Clock CP (.out(CP_out));
  rising_edge_D_FF rising_edge_d_ff_1 (
    .Q(Q2), .C(CP_out), .D(n4_sn1_1_q2), .S(n4_sn2_1_s2), .R(n4_sn2_1_r2), .Enable(1'b1));  // open: nQ
  rising_edge_D_FF rising_edge_d_ff_2 (
    .Q(Q1), .C(CP_out), .D(n4_sn1_1_q1), .S(n4_sn2_1_s1), .R(n4_sn2_1_r1), .Enable(1'b1));  // open: nQ
  rising_edge_D_FF rising_edge_d_ff_3 (
    .Q(Q0), .C(CP_out), .D(n4_sn1_1_q0), .S(n4_sn2_1_s0), .R(n4_sn2_1_r0), .Enable(1'b1));  // open: nQ
endmodule

module _4__SN1 (
  input  E2,
  input  E1,
  input  E0,
  input  FB,
  output Q2,
  output Q1,
  output Q0
);

  wire and_1_out, and_2_out, and_3_out, and_4_out, and_5_out, and_6_out, and_7_out, and_8_out, and_9_out,
       not_1_out, not_2_out, not_3_out, not_4_out, not_5_out, not_6_out, not_7_out, not_8_out, not_9_out,
       not_10_out, not_11_out, not_12_out, not_13_out, not_14_out, not_15_out;

  not not_1 (not_1_out, E2);
  not not_2 (not_2_out, E1);
  not not_3 (not_3_out, FB);
  not not_4 (not_4_out, E1);
  not not_5 (not_5_out, E0);
  not not_6 (not_6_out, E2);
  not not_7 (not_7_out, E1);
  not not_8 (not_8_out, FB);
  not not_9 (not_9_out, E1);
  not not_10 (not_10_out, E0);
  and and_1 (and_1_out, not_10_out, FB);
  not not_11 (not_11_out, E2);
  and and_2 (and_2_out, not_11_out, E0, not_12_out);
  not not_12 (not_12_out, FB);
  not not_13 (not_13_out, E1);
  and and_3 (and_3_out, not_13_out, not_14_out);
  not not_14 (not_14_out, FB);
  not not_15 (not_15_out, E0);
  and and_4 (and_4_out, E1, FB);
  and and_5 (and_5_out, not_1_out, not_2_out, not_3_out);
  and and_6 (and_6_out, not_4_out, not_5_out);
  and and_7 (and_7_out, not_6_out, E1, E0, FB);
  and and_8 (and_8_out, E2, not_7_out, FB);
  and and_9 (and_9_out, E2, E1, not_8_out);
  or or_1 (Q1, not_9_out, and_1_out, and_2_out);
  or or_2 (Q0, and_3_out, not_15_out, and_4_out, E2);
  or or_3 (Q2, and_5_out, and_6_out, and_7_out, and_8_out, and_9_out);
endmodule

module _4__SN2 (
  input  FB,
  input  R,
  output S2,
  output S1,
  output S0,
  output R2,
  output R1,
  output R0
);

  wire not_1_out, not_2_out;

  not not_1 (not_1_out, FB);
  not not_2 (not_2_out, FB);
  and and_1 (R2, FB, R);
  and and_2 (R1, FB, R);
  and and_3 (S2, not_1_out, R);
  and and_4 (S1, not_2_out, R);

  assign R0 = 1'b0;
  assign S0 = R;
endmodule

module _4_bit_mod_counter (
  input  S,
  input  R,
  input  En,
  input  CP,
  output Q3,
  output Q2,
  output Q1,
  output Q0,
  output nQ3,
  output nQ2,
  output nQ1,
  output nQ0
);

  wire undriven, undriven_2, undriven_3, undriven_4, undriven_5, undriven_6, undriven_7, undriven_8,
       undriven_9, undriven_10, undriven_11, undriven_12;

  LED D3 (.in(undriven));
  LED D2 (.in(undriven_12));
  LED D1 (.in(undriven_2));
  LED D0 (.in(undriven_3));
  onPosEdge onposedge_1 ();
  rising_edge_D_FF rising_edge_d_ff_1 (
    .Q(Q3), .C(CP), .D(undriven), .S(undriven_4), .R(undriven_8), .Enable(1'b1), .nQ(nQ3));
  rising_edge_D_FF rising_edge_d_ff_2 (
    .Q(Q2), .C(CP), .D(undriven_12), .S(undriven_5), .R(undriven_9), .Enable(1'b1), .nQ(nQ2));
  rising_edge_D_FF rising_edge_d_ff_3 (
    .Q(Q1), .C(CP), .D(undriven_2), .S(undriven_6), .R(undriven_10), .Enable(1'b1), .nQ(nQ1));
  rising_edge_D_FF rising_edge_d_ff_4 (
    .Q(Q0), .C(CP), .D(undriven_3), .S(undriven_7), .R(undriven_11), .Enable(1'b1), .nQ(nQ0));
endmodule

module rising_edge_D_FF (
  input  C,
  input  D,
  input  S,
  input  Enable,
  input  R,
  output Q,
  output nQ
);

  D_Flip_Flop d_ff_1 (.clk(C), .D(D), .Q(Q), .Qn(nQ), .preset(S), .en(Enable), .reset(R));
endmodule

module rising_edge_D_FF_mirrored (
  input  C,
  input  D,
  input  S,
  input  Enable,
  input  R,
  output Q,
  output nQ
);

  D_Flip_Flop d_ff_1 (.clk(C), .D(D), .Q(Q), .Qn(nQ), .preset(S), .en(Enable), .reset(R));
endmodule

module onPosEdge (
);


  // Notes on the sheet:
  //   Positive edge symbol
endmodule

module arrow (
);


  // Notes on the sheet:
  //   Arrow
endmodule
