// Logisim project 4_2_1.circ as structural Verilog: 4 circuits, main circuit D-FF
module _1__main (
  input  FB,
  input  R,
  input  S,
  output Q2,
  output Q1,
  output Q0,
  output F2,
  output F1,
  output F0
);

  wire C_out, n1_s1_1_q0_1, n1_s1_1_q1_1, n1_s1_1_q2_1;

  _1__S1 u_1_s1_1 (.D2(Q2), .D1(Q1), .D0(Q0), .FB(FB), .Q2_1(n1_s1_1_q2_1), .Q1_1(n1_s1_1_q1_1), .Q0_1(n1_s1_1_q0_1));
  Clock C (.out(C_out));
  D_FF d_ff_1 (.D(n1_s1_1_q2_1), .C(C_out), .E(1'b1), .Q(Q2));  // open: S, R
  D_FF d_ff_2 (.D(n1_s1_1_q1_1), .C(C_out), .E(1'b1), .Q(Q1));  // open: S, R
  D_FF d_ff_3 (.D(n1_s1_1_q0_1), .C(C_out), .E(1'b1), .Q(Q0));  // open: S, R
  _1__S2 u_1_s2_1 (.Q2(Q2), .Q1(Q1), .Q0(Q0), .F2(F2), .F1(F1), .F0(F0));
endmodule

module _1__S1 (
  input  D2,
  input  D1,
  input  D0,
  input  FB,
  output Q2_1,
  output Q1_1,
  output Q0_1
);

  wire and_1_out, and_2_out, and_3_out, and_4_out, and_5_out, and_6_out, and_7_out, and_8_out, and_9_out,
       not_1_out, not_2_out, not_3_out, not_4_out, not_5_out, not_6_out, not_7_out, not_8_out, not_9_out,
       not_10_out, not_11_out, not_12_out;

  not not_1 (not_1_out, D2);
  not not_2 (not_2_out, D1);
  not not_3 (not_3_out, D0);
  not not_4 (not_4_out, FB);
  not not_5 (not_5_out, D1);
  and and_1 (and_1_out, not_5_out, D0, FB);
  not not_6 (not_6_out, D0);
  and and_2 (and_2_out, D1, not_6_out, FB);
  and and_3 (and_3_out, D1, D0, not_7_out);
  not not_7 (not_7_out, FB);
  and and_4 (and_4_out, D2, not_8_out);
  not not_8 (not_8_out, FB);
  not not_9 (not_9_out, D2);
  and and_5 (and_5_out, not_9_out, not_10_out, FB);
  not not_10 (not_10_out, D0);
  and and_6 (and_6_out, D1, not_11_out);
  not not_11 (not_11_out, D0);
  and and_7 (and_7_out, D2, not_12_out);
  not not_12 (not_12_out, FB);
  and and_8 (and_8_out, not_1_out, not_2_out, not_3_out, not_4_out);
  or or_1 (Q2_1, and_8_out, and_9_out);
  and and_9 (and_9_out, D1, D0, FB);
  or or_2 (Q1_1, and_1_out, and_2_out, and_3_out, and_4_out);
  or or_3 (Q0_1, and_5_out, and_6_out, and_7_out);
endmodule

module _1__S2 (
  input  Q2,
  input  Q1,
  input  Q0,
  output F2,
  output F1,
  output F0
);

  or or_1 (F0, ~Q1, Q0);  // OR_Gate

  assign F1 = Q1;
  assign F2 = Q2;
endmodule

module D_FF (
  input  C,
  input  D,
  input  S,
  input  E,
  input  R,
  output Q
);

  D_Flip_Flop d_ff_1 (.clk(C), .D(D), .Q(Q), .preset(S), .en(E), .reset(R));  // open: Qn
endmodule
