// Logisim project tristateAndBus.circ as structural Verilog
module TristateBuffer (
  input  D,
  input  E,
  output Y,
  output Y_2,
  output Y_3,
  output Y_4,
  output Y_5
);

  assign Y = 1'b0 ? 1'b0 : 1'bz;  // Controlled_Buffer controlled_buffer_1
  assign Y_3 = 1'b1 ? 1'b0 : 1'bz;  // Controlled_Buffer controlled_buffer_2
  assign Y_5 = E ? D : 1'bz;  // Controlled_Buffer controlled_buffer_3
  table1 table1_1 ();
  assign Y_2 = 1'b0 ? 1'b1 : 1'bz;  // Controlled_Buffer controlled_buffer_4
  assign Y_4 = 1'b1 ? 1'b1 : 1'bz;  // Controlled_Buffer controlled_buffer_5

  // Notes on the sheet:
  //   D in beiden Fällen von Y entkoppelt (Schalter offen)
  //   D
  //   D an Y gekoppelt (Schalter geschlossen)
  //   D
  //   Playground
  //   E
  //   E
  //   D
  //   D
  //   E
  //   E
endmodule

module TristateMUX (
  input  A,
  input  B,
  input  Select,
  input  A_2,
  input  B_2,
  input  Select_2,
  input  A_3,
  input  B_3,
  input  Select_3,
  input  E,
  output Y_Z____Three_state__floating,
  output Y,
  output Y_2
);

  Multiplexer multiplexer_1 (.in0(A), .in1(B), .out(Y_Z____Three_state__floating), .sel(Select), .en(1'b0));
  Multiplexer multiplexer_2 (.in0(A_2), .in1(B_2), .out(Y), .sel(Select_2), .en(1'b1));
  Multiplexer multiplexer_3 (.in0(A_3), .in1(B_3), .out(Y_2), .sel(Select_3), .en(E));
  table2 table2_1 ();

  // Notes on the sheet:
  //   Multiplexer mit Tristate-Ausgang
  //   Playground
  //   E
  //   E
endmodule

module Busleitung_en_und_Teilnehmer (
  input  in_1,
  input  in_2,
  input  in_3,
  input  ROM1,
  input  Send,
  input  Receive,
  input  Send_2,
  input  Receive_2,
  input  Send_3,
  input  Receive_3,
  input  Send_4,
  input  [3:0] in_12,
  input  [3:0] in_13,
  input  [3:0] in_14,
  input  [3:0] ROM1_2,
  input  Send_5,
  input  Receive_4,
  input  Send_6,
  input  Receive_5,
  input  Send_7,
  input  Receive_6,
  input  Send_8,
  output out_23,
  output out_24,
  output out_25,
  output [3:0] out_26,
  output [3:0] out_27,
  output [3:0] out_28
);

  wire controlled_buffer_1_out;
  wire [3:0] controlled_buffer_2_out;

  line1 line1_1 ();
  line2 line2_1 ();
  assign controlled_buffer_1_out = Send ? in_1 : 1'bz;  // Controlled_Buffer controlled_buffer_1
  line1 line1_2 ();
  line2 line2_2 ();
  line1 line1_3 ();
  assign controlled_buffer_2_out = Send_5 ? in_12 : 4'bz;  // Controlled_Buffer controlled_buffer_2
  line1 line1_4 ();
  line2 line2_3 ();
  assign out_23 = Receive ? controlled_buffer_1_out : 1'bz;  // Controlled_Buffer controlled_buffer_3
  line2 line2_4 ();
  assign out_26 = Receive_4 ? controlled_buffer_2_out : 4'bz;  // Controlled_Buffer controlled_buffer_4
  line2 line2_5 ();
  line1 line1_5 ();
  line1 line1_6 ();
  line1 line1_7 ();
  line2 line2_6 ();
  line1 line1_8 ();
  assign out_24 = Receive_2 ? controlled_buffer_1_out : 1'bz;  // Controlled_Buffer controlled_buffer_5
  assign controlled_buffer_1_out = Send_2 ? in_2 : 1'bz;  // Controlled_Buffer controlled_buffer_6
  assign out_27 = Receive_5 ? controlled_buffer_2_out : 4'bz;  // Controlled_Buffer controlled_buffer_7
  assign controlled_buffer_2_out = Send_6 ? in_13 : 4'bz;  // Controlled_Buffer controlled_buffer_8
  line2 line2_7 ();
  line2 line2_8 ();
  line2 line2_9 ();
  line1 line1_9 ();
  assign out_25 = Receive_3 ? controlled_buffer_1_out : 1'bz;  // Controlled_Buffer controlled_buffer_9
  assign controlled_buffer_1_out = Send_3 ? in_3 : 1'bz;  // Controlled_Buffer controlled_buffer_10
  line1 line1_10 ();
  line1 line1_11 ();
  line2 line2_10 ();
  assign out_28 = Receive_6 ? controlled_buffer_2_out : 4'bz;  // Controlled_Buffer controlled_buffer_11
  assign controlled_buffer_2_out = Send_7 ? in_14 : 4'bz;  // Controlled_Buffer controlled_buffer_12
  line1 line1_12 ();
  line2 line2_11 ();
  line2 line2_12 ();
  line2 line2_13 ();
  line1 line1_13 ();
  assign controlled_buffer_1_out = Send_4 ? ROM1 : 1'bz;  // Controlled_Buffer controlled_buffer_13
  line1 line1_14 ();
  line2 line2_14 ();
  line1 line1_15 ();
  assign controlled_buffer_2_out = Send_8 ? ROM1_2 : 4'bz;  // Controlled_Buffer controlled_buffer_14
  line1 line1_16 ();
  line2 line2_15 ();
  line2 line2_16 ();

  // Notes on the sheet:
  //   CPU
  //   CPU
  //   gemeinsame Busleitung
  //   4 gemeinsame Busleitungen
  //   RAM1
  //   RAM1
  //   RAM2
  //   RAM2
endmodule

module _1_Bit_RAM__D_FF (
  input  Data,
  input  CoupleDataToBus,
  input  nSelectChip,
  input  nEnableOutput,
  input  Read_nWrite
);

  wire and_1_out, and_2_out, controlled_buffer_1_out, controlled_buffer_2_out, d_ff_1_q, nand_1_out,
       not_1_out, not_2_out, not_3_out;

  assign controlled_buffer_1_out = CoupleDataToBus ? Data : 1'bz;  // Controlled_Buffer controlled_buffer_1
  redLine redline_1 ();
  redLine redline_2 ();
  LED led_1 (.in(controlled_buffer_1_out));
  redLine redline_3 ();
  redLine redline_4 ();
  redLine redline_5 ();
  not not_1 (not_1_out, nSelectChip);
  redLine redline_6 ();
  redLine redline_7 ();
  assign controlled_buffer_2_out = and_1_out ? controlled_buffer_1_out : 1'bz;  // Controlled_Buffer controlled_buffer_2
  and and_1 (and_1_out, not_1_out, nEnableOutput);
  not not_2 (not_2_out, Read_nWrite);
  redLine redline_8 ();
  redLine redline_9 ();
  assign controlled_buffer_1_out = and_2_out ? d_ff_1_q : 1'bz;  // Controlled_Buffer controlled_buffer_3
  nand nand_1 (nand_1_out, not_1_out, not_2_out);
  and and_2 (and_2_out, not_1_out, not_3_out);
  not not_3 (not_3_out, nEnableOutput);
  redLine redline_10 ();
  redLine redline_11 ();
  D_Flip_Flop d_ff_1 (.clk(nand_1_out), .D(controlled_buffer_2_out), .Q(d_ff_1_q));  // open: Qn, preset, en, reset
  redLine redline_12 ();
  redLine redline_13 ();
  redLine redline_14 ();
  redLine redline_15 ();
  redLine redline_16 ();
  redLine redline_17 ();
  redLine redline_18 ();

  // Notes on the sheet:
  //   1-Bit RAM mit D-FF realisiert
  //   Schreiben in das 1-Bit-RAM
  //   1. Vorbedingungen: ~CS=1. ~OE=1, R/~W=1, CoupleDataToBus=1
  //   2. Chip Select: ~CS=0
  //   3. Schreiben vorbereiten: R/~W=0
  //   4. Datum definieren: Data=0 oder Data=1
  //   5. Schreiben auf steigende Flanke: R/~W=1
  //   6. Chip Selekt deaktivieren: ~CS=1
  //   Bidirectional Bus
  //   ~CS
  //   ~OE
  //   RD/~WR
  //   Lesen aus dem 1-Bit RAM
  //   1. Vorbedingungen: ~CS=1. ~OE=1, R/~W=1, CoupleDataToBus=0
  //   2. Chip Select: ~CS=0
  //   3. Output aktivieren: ~OE=0
  //   4. Datum auslesen
  //   5. Output deaktivieren: ~OE=1
  //   6. Chip Selekt deaktivieren: ~CS=1
  //   1-Bit RAM
endmodule

module _2x_1_Bit_RAM__D_FFs (
);

  wire and_1_out, and_2_out, and_3_out, and_4_out, button_1_out, controlled_buffer_1_out,
       controlled_buffer_2_out, controlled_buffer_4_out, Couple, d_ff_1_q, d_ff_2_q, Data, nand_1_out,
       nand_2_out, nEO, not_1_out, not_2_out, not_3_out, not_4_out, not_5_out, not_6_out, nS0, nS1, R_nW;
  wire [5:0] counter_1_q;

  Button button_1 (.out(button_1_out));
  Counter #(.width(6), .max('h1d)) counter_1 (
    .load(1'b0), .count(1'b1), .Q(counter_1_q), .clk(button_1_out));  // open: D, carry, clr
  ROM #(.addrWidth(6), .dataWidth(6)) rom_1 (
    .addr(counter_1_q), .data({Data, Couple, nS0, nEO, R_nW, nS1}));  // open: sel
  assign controlled_buffer_1_out = Couple ? Data : 1'bz;  // Controlled_Buffer controlled_buffer_1
  LED led_1 (.in(controlled_buffer_1_out));
  redLine redline_1 ();
  redLine redline_2 ();
  redLine redline_3 ();
  redLine redline_4 ();
  redLine redline_5 ();
  redLine redline_6 ();
  redLine redline_7 ();
  redLine redline_8 ();
  redLine redline_9 ();
  and and_1 (and_1_out, not_1_out, nEO);
  not not_1 (not_1_out, nS0);
  not not_2 (not_2_out, R_nW);
  redLine redline_10 ();
  redLine redline_11 ();
  and and_2 (and_2_out, not_3_out, nEO);
  not not_3 (not_3_out, nS1);
  not not_4 (not_4_out, R_nW);
  redLine redline_12 ();
  redLine redline_13 ();
  assign controlled_buffer_2_out = and_1_out ? controlled_buffer_1_out : 1'bz;  // Controlled_Buffer controlled_buffer_2
  assign controlled_buffer_1_out = and_3_out ? d_ff_1_q : 1'bz;  // Controlled_Buffer controlled_buffer_3
  and and_3 (and_3_out, not_1_out, not_5_out);
  not not_5 (not_5_out, nEO);
  redLine redline_14 ();
  redLine redline_15 ();
  assign controlled_buffer_4_out = and_2_out ? controlled_buffer_1_out : 1'bz;  // Controlled_Buffer controlled_buffer_4
  assign controlled_buffer_1_out = and_4_out ? d_ff_2_q : 1'bz;  // Controlled_Buffer controlled_buffer_5
  and and_4 (and_4_out, not_3_out, not_6_out);
  not not_6 (not_6_out, nEO);
  redLine redline_16 ();
  redLine redline_17 ();
  nand nand_1 (nand_1_out, not_1_out, not_2_out);
  redLine redline_18 ();
  redLine redline_19 ();
  nand nand_2 (nand_2_out, not_3_out, not_4_out);
  redLine redline_20 ();
  redLine redline_21 ();
  D_Flip_Flop d_ff_1 (.clk(nand_1_out), .D(controlled_buffer_2_out), .Q(d_ff_1_q));  // open: Qn, preset, en, reset
  redLine redline_22 ();
  redLine redline_23 ();
  D_Flip_Flop d_ff_2 (.clk(nand_2_out), .D(controlled_buffer_4_out), .Q(d_ff_2_q));  // open: Qn, preset, en, reset
  redLine redline_24 ();
  redLine redline_25 ();
  redLine redline_26 ();
  redLine redline_27 ();
  redLine redline_28 ();
  redLine redline_29 ();
  redLine redline_30 ();
  redLine redline_31 ();
  redLine redline_32 ();
  redLine redline_33 ();
  redLine redline_34 ();
  redLine redline_35 ();
  redLine redline_36 ();

  // Notes on the sheet:
  //   Zwei 1-Bit RAM mit D-FFs realisiert
  //   contents of rom_1 (hex, n*v repeats v):
  //   1 5 25 35 37 3f 3e 3c 3e 1e e f 7 3 7 5 15 17 1f f e a e 1e 1c 1e e a 8
  //   Bidirectional Bus
  //   ~CS
  //   ~OE
  //   RD/~WR
  //   ~CS
  //   ~OE
  //   RD/~WR
  //   1-Bit RAM 0
  //   1-Bit RAM 1
endmodule

module _1_Bit_RAM__Library_RAM (
  input  Data,
  input  CoupleDataToBus,
  input  nSelectChip,
  input  nEnableOutput,
  input  Read_nWrite
);

  wire controlled_buffer_1_out, controlled_buffer_2_out, not_1_out, not_2_out;

  assign controlled_buffer_1_out = CoupleDataToBus ? Data : 1'bz;  // Controlled_Buffer controlled_buffer_1
  redLine redline_1 ();
  redLine redline_2 ();
  redLine redline_3 ();
  LED led_1 (.in(controlled_buffer_1_out));
  redLine redline_4 ();
  redLine redline_5 ();
  not not_1 (not_1_out, nSelectChip);
  redLine redline_6 ();
  redLine redline_7 ();
  assign controlled_buffer_2_out = nEnableOutput ? controlled_buffer_1_out : 1'bz;  // Controlled_Buffer controlled_buffer_2
  not not_2 (not_2_out, nEnableOutput);
  redLine redline_8 ();
  redLine redline_9 ();
  assign controlled_buffer_1_out = not_2_out ? controlled_buffer_2_out : 1'bz;  // Controlled_Buffer controlled_buffer_3
  redLine redline_10 ();
  redLine redline_11 ();
  RAM #(.addrWidth(2), .dataWidth(1)) ram_1 (
    .addr(2'b00), .data(controlled_buffer_2_out), .sel(not_1_out), .clk(Read_nWrite), .ld(not_2_out));  // open: clr
  redLine redline_12 ();
  redLine redline_13 ();
  redLine redline_14 ();
  redLine redline_15 ();
  redLine redline_16 ();
  redLine redline_17 ();
  redLine redline_18 ();

  // Notes on the sheet:
  //   1-Bit RAM mit Library RAM (fixe Adresse 0) realisiert
  //   Schreiben in das 1-Bit-RAM
  //   1. Vorbedingungen: ~CS=1. ~OE=1, R/~W=1, CoupleDataToBus=1
  //   2. Chip Select: ~CS=0
  //   3. Schreiben vorbereiten: R/~W=0
  //   4. Datum definieren: Data=0 oder Data=1
  //   5. Schreiben auf steigende Flanke: R/~W=1
  //   6. Chip Selekt deaktivieren: ~CS=1
  //   Bidirectional Bus
  //   ~CS
  //   ~OE
  //   RD/~WR
  //   Lesen aus dem 1-Bit RAM
  //   1. Vorbedingungen: ~CS=1. ~OE=1, R/~W=1, CoupleDataToBus=0
  //   2. Chip Select: ~CS=0
  //   3. Output aktivieren: ~OE=0
  //   4. Datum auslesen
  //   5. Output deaktivieren: ~OE=1
  //   6. Chip Selekt deaktivieren: ~CS=1
  //   1-Bit RAM
endmodule

module _2x_1_Bit_RAM__Library_RAMs (
  input  Data,
  input  CoupleDataToBus,
  input  nSelectChip0,
  input  nEnableOutput,
  input  Read_nWrite,
  input  nSelectChip1
);

  wire controlled_buffer_1_out, controlled_buffer_2_out, controlled_buffer_3_out, not_1_out, not_2_out,
       not_3_out, not_4_out;

  assign controlled_buffer_1_out = CoupleDataToBus ? Data : 1'bz;  // Controlled_Buffer controlled_buffer_1
  redLine redline_1 ();
  redLine redline_2 ();
  redLine redline_3 ();
  redLine redline_4 ();
  redLine redline_5 ();
  redLine redline_6 ();
  LED led_1 (.in(controlled_buffer_1_out));
  redLine redline_7 ();
  redLine redline_8 ();
  redLine redline_9 ();
  not not_1 (not_1_out, nSelectChip0);
  redLine redline_10 ();
  redLine redline_11 ();
  not not_2 (not_2_out, nSelectChip1);
  redLine redline_12 ();
  redLine redline_13 ();
  assign controlled_buffer_2_out = nEnableOutput ? controlled_buffer_1_out : 1'bz;  // Controlled_Buffer controlled_buffer_2
  not not_3 (not_3_out, nEnableOutput);
  redLine redline_14 ();
  redLine redline_15 ();
  assign controlled_buffer_3_out = nEnableOutput ? controlled_buffer_1_out : 1'bz;  // Controlled_Buffer controlled_buffer_3
  not not_4 (not_4_out, nEnableOutput);
  redLine redline_16 ();
  redLine redline_17 ();
  assign controlled_buffer_1_out = not_3_out ? controlled_buffer_2_out : 1'bz;  // Controlled_Buffer controlled_buffer_4
  redLine redline_18 ();
  redLine redline_19 ();
  assign controlled_buffer_1_out = not_4_out ? controlled_buffer_3_out : 1'bz;  // Controlled_Buffer controlled_buffer_5
  redLine redline_20 ();
  redLine redline_21 ();
  RAM #(.addrWidth(2), .dataWidth(1)) ram_1 (
    .addr(2'b00), .data(controlled_buffer_2_out), .sel(not_1_out), .clk(Read_nWrite), .ld(not_3_out));  // open: clr
  redLine redline_22 ();
  redLine redline_23 ();
  RAM #(.addrWidth(2), .dataWidth(1)) ram_2 (
    .addr(2'b00), .data(controlled_buffer_3_out), .sel(not_2_out), .clk(Read_nWrite), .ld(not_4_out));  // open: clr
  redLine redline_24 ();
  redLine redline_25 ();
  redLine redline_26 ();
  redLine redline_27 ();
  redLine redline_28 ();
  redLine redline_29 ();
  redLine redline_30 ();
  redLine redline_31 ();
  redLine redline_32 ();
  redLine redline_33 ();
  redLine redline_34 ();
  redLine redline_35 ();
  redLine redline_36 ();

  // Notes on the sheet:
  //   Zwei 1-Bit RAM mit Library RAMs (fixe Adressen 0) realisiert
  //   Bidirectional Bus
  //   ~CS
  //   ~OE
  //   RD/~WR
  //   ~CS
  //   ~OE
  //   RD/~WR
  //   1-Bit RAM 0
  //   1-Bit RAM 1
endmodule

module table1 (
);


  // Notes on the sheet:
  //   Table 1
endmodule

module table2 (
);


  // Notes on the sheet:
  //   Table 2
endmodule
