// Logisim project 5_2.circ as structural Verilog: 5 circuits, main circuit SN1
module main (
  input  [3:0] Ziffer
);

  wire OK_out, sn2_1_y;
  wire [1:0] sn1_1_z_1, Zustand;

  Button OK (.out(OK_out));
  SN1 sn1_1 (.Z(Zustand), .Z_1(sn1_1_z_1), .E(Ziffer));
  MEM mem_1 (.Pulse(OK_out), .D(sn1_1_z_1), .out_3(Zustand));
  LED nLocked_Open (.in(sn2_1_y));
  SN2 sn2_1 (.Z(Zustand), .Y(sn2_1_y));
  Hex_Digit_Display hex_digit_display_1 (.value({2'b00, Zustand}));  // open: dp
endmodule

module SN1 (
  input  [1:0] Z,
  input  [3:0] E,
  output [1:0] Z_1
);

  ROM #(.addrWidth(6), .dataWidth(2)) rom_1 (.addr({E, Z}), .data(Z_1));  // open: sel

  // Notes on the sheet:
  //   contents of rom_1 (hex, n*v repeats v):
  //   8*0 1 0 3 18*0 2
endmodule

module MEM (
  input  Pulse,
  input  [1:0] D,
  output [1:0] out_3
);

  D_Flip_Flop d_ff_1 (.clk(Pulse), .D(D[0]), .Q(out_3[0]));  // open: Qn, preset, en, reset
  D_Flip_Flop d_ff_2 (.clk(Pulse), .D(D[1]), .Q(out_3[1]));  // open: Qn, preset, en, reset
endmodule

module SN2 (
  input  [1:0] Z,
  output Y
);

  ROM #(.addrWidth(2), .dataWidth(1)) rom_1 (.addr(Z), .data(Y));  // open: sel

  // Notes on the sheet:
  //   contents of rom_1 (hex, n*v repeats v):
  //   0 0 0 1
endmodule

module alternative (
  input  [3:0] Ziffer,
  output [1:0] Z_1
);

  wire OK_out;
  wire [1:0] Zustand;
  wire [2:2] rom_1_data;

  Button OK (.out(OK_out));
  MEM mem_1 (.Pulse(OK_out), .D(Z_1), .out_3(Zustand));
  ROM #(.addrWidth(6), .dataWidth(3)) rom_1 (.addr({Ziffer, Zustand}), .data({rom_1_data[2], Z_1}));  // open: sel
  LED nLocked_Open (.in(rom_1_data[2]));
  Hex_Digit_Display hex_digit_display_1 (.value({2'b00, Zustand}));  // open: dp

  // Notes on the sheet:
  //   contents of rom_1 (hex, n*v repeats v):
  //   8*0 1 0 3 4 17*0 2
endmodule
