// Logisim project 2_2.circ as structural Verilog: 6 circuits, main circuit 1_c
module _1_a (
  input  x2,
  input  x1,
  input  x0,
  output out_4
);

  wire and_1_out, and_2_out, and_3_out;

  and and_1 (and_1_out, ~x0, x1, ~x2);  // AND_Gate
  and and_2 (and_2_out, ~x0, x1, x2);  // AND_Gate
  and and_3 (and_3_out, x0, x1, x2);
  or or_1 (out_4, and_1_out, and_2_out, and_3_out);
endmodule

module _1_c (
  input  x2,
  input  x1,
  input  x0,
  output out_4
);

  wire or_1_out;

  or or_1 (or_1_out, x2, ~x0);  // OR_Gate
  and and_1 (out_4, or_1_out, x1);
endmodule

module _1_d (
  input  x2,
  input  x1,
  input  x0,
  output y
);

  wire and_1_out, and_2_out, not_1_out;

  not not_1 (not_1_out, x0);
  and and_1 (and_1_out, x1, not_1_out);
  and and_2 (and_2_out, x2, x1);
  or or_1 (y, and_1_out, and_2_out);
endmodule

module _2 (
  input  x4,
  input  x3,
  input  x2,
  input  x1,
  input  x0,
  output x
);

  wire and_1_out, and_2_out, and_3_out, and_4_out, not_1_out, not_2_out;

  not not_1 (not_1_out, x2);
  not not_2 (not_2_out, x1);
  and and_1 (and_1_out, not_1_out, x0);
  and and_2 (and_2_out, not_2_out, x0);
  and and_3 (and_3_out, x3, x0);
  and and_4 (and_4_out, x4, x0);
  or or_1 (x, and_1_out, and_2_out, and_3_out, and_4_out);
endmodule

module _3 (
  input  x2,
  input  x1,
  input  x0
);

  wire and_1_out, and_2_out, or_1_out, or_2_out, or_3_out, or_4_out;

  or or_1 (or_1_out, x2, x1);
  LED led_1 (.in(or_1_out));
  LED led_2 (.in(or_1_out));
  LED led_3 (.in(or_1_out));
  or or_2 (or_2_out, x2, x0);
  LED led_4 (.in(or_2_out));
  LED led_5 (.in(or_2_out));
  LED led_6 (.in(or_2_out));
  LED led_7 (.in(or_4_out));
  LED led_8 (.in(or_3_out));
  LED led_9 (.in(or_3_out));
  LED led_10 (.in(or_3_out));
  or or_3 (or_3_out, x2, and_1_out);
  and and_1 (and_1_out, x0, ~x1);  // AND_Gate
  LED led_11 (.in(or_4_out));
  or or_4 (or_4_out, x2, and_2_out);
  LED led_12 (.in(or_4_out));
  and and_2 (and_2_out, x1, ~x0);  // AND_Gate

  // Notes on the sheet:
  //   a
  //   d
  //   b
  //   c
endmodule

module _3_mintest (
  input  x2,
  input  x1,
  input  x0,
  output y1,
  output y2
);

  wire and_1_out, and_2_out, and_3_out, or_1_out;

  and and_1 (and_1_out, ~x2, x1);  // AND_Gate
  and and_2 (and_2_out, x2, ~x1);  // AND_Gate
  and and_3 (and_3_out, x1, ~x0);  // AND_Gate
  or or_1 (or_1_out, and_1_out, and_2_out);
  and and_4 (y1, or_1_out, ~x0);  // AND_Gate
  or or_2 (y2, and_3_out, x2);
endmodule
