// Logisim project 3_1.circ as structural Verilog: 7 circuits, main circuit 1c_opt
module _1c_opt (
  input  X3,
  input  X2,
  input  X1,
  input  X0,
  output Y1,
  output Y0
);

  wire and_1_out, and_2_out, and_3_out, and_4_out, and_5_out, and_6_out, and_7_out, and_8_out, and_9_out,
       and_10_out, not_1_out, not_2_out, not_3_out, not_4_out, not_5_out, not_6_out, not_7_out, not_8_out,
       not_9_out, not_10_out, not_11_out, not_12_out, not_13_out, not_14_out, not_15_out, not_16_out,
       not_17_out, not_18_out, not_19_out, not_20_out;

  not not_1 (not_1_out, X3);
  not not_2 (not_2_out, X2);
  not not_3 (not_3_out, X0);
  not not_4 (not_4_out, X3);
  not not_5 (not_5_out, X1);
  not not_6 (not_6_out, X2);
  not not_7 (not_7_out, X1);
  not not_8 (not_8_out, X0);
  not not_9 (not_9_out, X2);
  not not_10 (not_10_out, X0);
  not not_11 (not_11_out, X3);
  not not_12 (not_12_out, X2);
  not not_13 (not_13_out, X1);
  not not_14 (not_14_out, X3);
  not not_15 (not_15_out, X1);
  not not_16 (not_16_out, X0);
  not not_17 (not_17_out, X3);
  not not_18 (not_18_out, X2);
  not not_19 (not_19_out, X0);
  not not_20 (not_20_out, X1);
  and and_1 (and_1_out, not_1_out, not_2_out, X1, not_3_out);
  and and_2 (and_2_out, not_4_out, X2, not_5_out, X0);
  and and_3 (and_3_out, X3, not_6_out, not_7_out, not_8_out);
  and and_4 (and_4_out, X3, not_9_out, X1, X0);
  and and_5 (and_5_out, X3, X2, X1, not_10_out);
  and and_6 (and_6_out, not_11_out, not_12_out, not_13_out, X0);
  and and_7 (and_7_out, not_14_out, X2, not_15_out, not_16_out);
  and and_8 (and_8_out, not_17_out, X2, X1, X0);
  and and_9 (and_9_out, X3, not_18_out, X1, not_19_out);
  and and_10 (and_10_out, X3, X2, not_20_out, X0);
  or or_1 (Y1, and_1_out, and_2_out, and_3_out, and_4_out, and_5_out);
  or or_2 (Y0, and_6_out, and_7_out, and_8_out, and_9_out, and_10_out);

  // Notes on the sheet:
  //   Modulo 3
endmodule

module _4_1_MUX (
  input  S1,
  input  S0,
  input  I0,
  input  I1,
  input  I2,
  input  I3,
  input  nEnable,
  output Y
);

  wire and_1_out, and_2_out, and_3_out, and_4_out, xor_1_out;

  and and_1 (and_1_out, ~S0, ~S1, I0);  // AND_Gate
  and and_2 (and_2_out, S0, ~S1, I1);  // AND_Gate
  and and_3 (and_3_out, S1, ~S0, I2);  // AND_Gate
  and and_4 (and_4_out, S1, S0, I3);
  ExactlyOne xor_1 (.out(xor_1_out), .in0(and_1_out), .in1(and_2_out), .in2(and_3_out), .in3(and_4_out));
  and and_5 (Y, xor_1_out, ~nEnable);  // AND_Gate

  // Notes on the sheet:
  //   4:1 MUX
endmodule

module _3_a (
  input  A3,
  input  A2,
  input  A1,
  input  A0,
  input  B0,
  output Y3,
  output Y2,
  output Y1,
  output Y0
);

  and and_1 (Y0, B0, A0);
  and and_2 (Y1, B0, A1);
  and and_3 (Y2, B0, A2);
  and and_4 (Y3, B0, A3);
endmodule

module _3_b (
  input  A3,
  input  A2,
  input  A1,
  input  A0,
  input  B3,
  input  B2,
  input  B1,
  input  B0,
  output C,
  output Y3,
  output Y2,
  output Y1,
  output Y0
);

  wire ha_1_c, va_1_cout, va_2_cout;

  HA ha_1 (.C(ha_1_c), .Y(Y0), .A(A0), .B(B0));
  VA va_1 (.Cout(va_1_cout), .Y(Y2), .Cin(va_2_cout), .A(A2), .B(B2));
  VA va_2 (.Cout(va_2_cout), .Y(Y1), .Cin(ha_1_c), .A(A1), .B(B1));
  VA va_3 (.Cout(C), .Y(Y3), .Cin(va_1_cout), .A(A3), .B(B3));

  // Notes on the sheet:
  //   4-Bit Addierer
endmodule

module _3_c (
  input  A3,
  input  A2,
  input  A1,
  input  A0,
  input  B3,
  input  B2,
  input  B1,
  input  B0,
  output C,
  output Y7,
  output Y6,
  output Y5,
  output Y4,
  output Y3,
  output Y2,
  output Y1,
  output Y0
);

  _3_a u_3_a_1 (.A3(A3), .A2(A1), .A1(A0), .A0(A0), .B0(B0), .Y0(Y0));  // open: Y3, Y2, Y1
  _3_a u_3_a_2 (.A3(A3), .A2(A2), .A1(A1), .A0(A0), .B0(B1));  // open: Y3, Y2, Y1, Y0
  _3_a u_3_a_3 (.A3(A3), .A2(A2), .A1(A1), .A0(A0), .B0(B2));  // open: Y3, Y2, Y1, Y0
  _3_a u_3_a_4 (.A3(A3), .A2(A2), .A1(A1), .A0(A0), .B0(B3));  // open: Y3, Y2, Y1, Y0
endmodule

module HA (
  input  A,
  input  B,
  output C,
  output Y
);

  xor xor_1 (Y, B, A);
  and and_1 (C, B, A);

  // Notes on the sheet:
  //   HA: Halbaddierer
endmodule

module VA (
  input  Cin,
  input  A,
  input  B,
  output Cout,
  output Y
);

  wire ha_1_c, ha_1_y, ha_2_c;

  HA ha_1 (.C(ha_1_c), .Y(ha_1_y), .A(B), .B(A));
  HA ha_2 (.C(ha_2_c), .Y(Y), .A(ha_1_y), .B(Cin));
  or or_1 (Cout, ha_1_c, ha_2_c);

  // Notes on the sheet:
  //   VA: Volladdierer
endmodule
