// Logisim project 4_2_2.circ as structural Verilog: 5 circuits, main circuit Aufgaben_4.2.2
module Aufgaben_4_2_2 (
  input  a,
  input  b
);

  wire clock_1_out, fsm_1_y0, fsm_1_y1, fsm_1_y2, Goto_0_out, Goto_1_out, sn2_1_led0, sn2_1_led1, sn2_1_led2,
       sn2_1_led3, sn2_1_led4, sn2_1_led5, sn2_1_led6, sn2_1_led7;

  Clock clock_1 (.out(clock_1_out));
  FSM fsm_1 (
    .a(a), .b(b), .CP(clock_1_out), .En(1'b1), .S(Goto_1_out), .R(Goto_0_out), .Y2(fsm_1_y2), .Y1(fsm_1_y1),
    .Y0(fsm_1_y0));
  Button Goto_1 (.out(Goto_1_out));
  Button Goto_0 (.out(Goto_0_out));
  SN2 sn2_1 (
    .LED7(sn2_1_led7), .LED6(sn2_1_led6), .LED5(sn2_1_led5), .LED4(sn2_1_led4), .LED3(sn2_1_led3),
    .LED2(sn2_1_led2), .LED1(sn2_1_led1), .LED0(sn2_1_led0), .Q2(fsm_1_y2), .Q1(fsm_1_y1), .Q0(fsm_1_y0));
  LED _6 (.in(sn2_1_led6));
  LED _4 (.in(sn2_1_led4));
  LED _0 (.in(sn2_1_led0));
  LED _2 (.in(sn2_1_led2));
  LED _7 (.in(sn2_1_led7));
  LED _3 (.in(sn2_1_led3));
  LED _5 (.in(sn2_1_led5));
  LED _1 (.in(sn2_1_led1));

  // Notes on the sheet:
  //   a=b=x
  //   a=b=x
  //   a=b=x
  //   a=0, b=x
  //   a=x, b=0
  //   a=x, b=1
  //   a=1, b=x
  //   a=b=x
  //   a=b=x
  //   a=b=x
endmodule

module FSM (
  input  a,
  input  b,
  input  En,
  input  S,
  input  R,
  input  CP,
  output Y0,
  output Y1,
  output Y2
);

  wire sn1_1_y0, sn1_1_y1, sn1_1_y2;

  SN1 sn1_1 (.A(a), .B(b), .X2(Y2), .X1(Y1), .X0(Y0), .Y2(sn1_1_y2), .Y1(sn1_1_y1), .Y0(sn1_1_y0));
  SP sp_1 (.X2(sn1_1_y2), .X1(sn1_1_y1), .X0(sn1_1_y0), .Y2(Y2), .Y1(Y1), .Y0(Y0), .CP(CP), .S(S), .R(R), .E(En));
endmodule

module SN1 (
  input  A,
  input  B,
  input  X2,
  input  X1,
  input  X0,
  output Y2,
  output Y1,
  output Y0
);

  wire and_1_out, and_2_out, and_3_out, and_4_out, and_5_out, and_6_out, and_7_out, and_8_out, and_9_out,
       not_1_out, not_2_out, not_3_out, not_4_out, not_5_out, not_6_out, not_7_out, not_8_out, not_9_out,
       not_10_out;

  not not_1 (not_1_out, X2);
  not not_2 (not_2_out, A);
  not not_3 (not_3_out, X2);
  not not_4 (not_4_out, X1);
  not not_5 (not_5_out, X2);
  not not_6 (not_6_out, X0);
  not not_7 (not_7_out, X2);
  not not_8 (not_8_out, X1);
  not not_9 (not_9_out, X2);
  and and_1 (and_1_out, not_1_out, X0);
  and and_2 (and_2_out, not_2_out, not_3_out, X1);
  and and_3 (and_3_out, X2, not_4_out);
  not not_10 (not_10_out, X1);
  and and_4 (and_4_out, B, X2, X0);
  and and_5 (and_5_out, A, not_5_out, not_6_out);
  and and_6 (and_6_out, not_7_out, X0);
  and and_7 (and_7_out, not_8_out, X0);
  and and_8 (and_8_out, B, X0);
  and and_9 (and_9_out, A, not_9_out, X1);
  or or_1 (Y2, and_1_out, and_2_out, and_3_out);
  or or_2 (Y1, not_10_out, and_4_out, and_5_out);
  or or_3 (Y0, and_6_out, and_7_out, and_8_out, and_9_out);
endmodule

module SP (
  input  CP,
  input  S,
  input  R,
  input  E,
  input  X2,
  input  X1,
  input  X0,
  output Y2,
  output Y1,
  output Y0
);

  wire or_1_out, or_2_out;

  or or_1 (or_1_out, S, R);
  or or_2 (or_2_out, S, R);
  D_Flip_Flop d_ff_1 (.clk(CP), .D(X2), .Q(Y2), .preset(1'b0), .en(E), .reset(or_1_out));  // open: Qn
  D_Flip_Flop d_ff_2 (.clk(CP), .D(X1), .Q(Y1), .preset(1'b0), .en(E), .reset(or_2_out));  // open: Qn
  D_Flip_Flop d_ff_3 (.clk(CP), .D(X0), .Q(Y0), .preset(S), .en(E), .reset(R));  // open: Qn
endmodule

module SN2 (
  input  Q0,
  input  Q1,
  input  Q2,
  output LED0,
  output LED1,
  output LED2,
  output LED3,
  output LED4,
  output LED5,
  output LED6,
  output LED7
);

  Decoder #(.select(3), .disabled(0), .enable("false")) decoder_1 (
    .out0(LED0), .out1(LED1), .out2(LED2), .out3(LED3), .out4(LED4), .out5(LED5), .out6(LED6), .out7(LED7),
    .sel({Q2, Q1, Q0}));
endmodule
