// Logisim project DFFs.circ as structural Verilog: 6 circuits, main circuit 4-Bit Memory
module _4_Bit_Memory (
  input  En,
  input  [3:0] S,
  input  [3:0] R,
  input  CP,
  input  D3,
  input  D2,
  input  D1,
  input  D0,
  output Q3,
  output nQ3,
  output Q2,
  output nQ2,
  output Q1,
  output nQ1,
  output Q0,
  output nQ0
);

  rising_edge_D_FF rising_edge_d_ff_1 (.Q(Q3), .C(CP), .D(D3), .S(S[3]), .R(R[3]), .Enable(En), .nQ(nQ3));
  rising_edge_D_FF rising_edge_d_ff_2 (.Q(Q2), .C(CP), .D(D2), .S(S[2]), .R(R[2]), .Enable(En), .nQ(nQ2));
  rising_edge_D_FF rising_edge_d_ff_3 (.Q(Q1), .C(CP), .D(D1), .S(S[1]), .R(R[1]), .Enable(En), .nQ(nQ1));
  rising_edge_D_FF rising_edge_d_ff_4 (.Q(Q0), .C(CP), .D(D0), .S(S[0]), .R(R[0]), .Enable(En), .nQ(nQ0));
endmodule

module _3_Bit_Memory (
  input  En,
  input  [2:0] S,
  input  [2:0] R,
  input  CP,
  input  D2,
  input  D1,
  input  D0,
  output Q2,
  output nQ2,
  output Q1,
  output nQ1,
  output Q0,
  output nQ0
);
endmodule

module rising_edge_D_FF (
  input  C,
  input  D,
  input  S,
  input  Enable,
  input  R,
  output Q,
  output nQ
);

  D_Flip_Flop d_ff_1 (.clk(C), .D(D), .Q(Q), .Qn(nQ), .preset(S), .en(Enable), .reset(R));
endmodule

module rising_edge_D_FF_mirrored (
  input  C,
  input  D,
  input  S,
  input  Enable,
  input  R,
  output Q,
  output nQ
);

  D_Flip_Flop d_ff_1 (.clk(C), .D(D), .Q(Q), .Qn(nQ), .preset(S), .en(Enable), .reset(R));
endmodule

module onPosEdge (
);


  // Notes on the sheet:
  //   Positive edge symbol
endmodule

module arrow (
);


  // Notes on the sheet:
  //   Arrow
endmodule
