// Logisim project 5_1_2.circ as structural Verilog: 2 circuits, main circuit main
module main (
  input  [1:0] Address,
  output out_2,
  output out_3,
  output out_4,
  output out_5
);

  ROM #(.addrWidth(2), .dataWidth(4)) rom_1 (.addr(Address), .data({out_2, out_3, out_4, out_5}));  // open: sel

  // Notes on the sheet:
  //   5.1.2: 4x4 ROM
  //   Lösung versteh ich nicht....
  //   contents of rom_1 (hex, n*v repeats v):
  //   1 3 5 7
endmodule

module b (
  input  A1,
  input  A0,
  input  I3,
  input  I2,
  input  I1,
  input  I0,
  output Y
);

  wire and_1_out, and_2_out, and_3_out, not_1_out, not_2_out, not_3_out, not_4_out, not_5_out, not_6_out,
       not_7_out;

  not not_1 (not_1_out, A0);
  not not_2 (not_2_out, I3);
  not not_3 (not_3_out, A0);
  not not_4 (not_4_out, I2);
  not not_5 (not_5_out, I1);
  not not_6 (not_6_out, I0);
  not not_7 (not_7_out, A1);
  and and_1 (and_1_out, not_1_out, not_2_out);
  and and_2 (and_2_out, not_3_out, not_4_out, not_5_out, not_6_out);
  and and_3 (and_3_out, A0, I3, I2, I1, I0);
  or or_1 (Y, not_7_out, and_1_out, and_2_out, and_3_out);
endmodule
